// Logisim project 24_bit_collatz.circ as structural Verilog: 1 circuit, main circuit main
module main (
);

  wire adder_2_cout, adder_3_cout, button_1_out, button_2_out, button_3_out, clock_1_out;
  wire [1:0] priority_encoder_1_out;
  wire [7:0] adder_1_out, adder_2_out, adder_3_out, register_1_q, register_2_q, register_3_q, rom_1_data;

  Button button_1 (.out(button_1_out));
  Button button_2 (.out(button_2_out));
  Button button_3 (.out(button_3_out));
  ROM #(.addrWidth(2)) rom_1 (.addr(priority_encoder_1_out), .data(rom_1_data));
  Priority_Encoder #(.select(2)) priority_encoder_1 (
    .in0(button_1_out), .in1(button_2_out), .in2(button_3_out), .out(priority_encoder_1_out));  // open: in3, gs, en_out, en_in
  Clock clock_1 (.out(clock_1_out));
  Register #(.trigger("high")) register_1 (
    .D(rom_1_data), .en(button_1_out), .clk(button_1_out), .Q(register_1_q));  // open: clr
  Register #(.trigger("high")) register_2 (
    .D(rom_1_data), .en(button_2_out), .clk(button_2_out), .Q(register_2_q));  // open: clr
  Register #(.trigger("high")) register_3 (
    .D(rom_1_data), .en(button_3_out), .clk(button_3_out), .Q(register_3_q));  // open: clr
  Adder adder_1 (
    .a({register_1_q[6:0], register_2_q[7]}), .b(register_1_q), .out(adder_1_out), .cin(adder_2_cout));  // open: cout
  Adder adder_2 (
    .a({register_2_q[6:0], register_3_q[7]}), .b(register_2_q), .out(adder_2_out), .cin(adder_3_cout),
    .cout(adder_2_cout));
  Adder adder_3 (.a({register_3_q[6:0], 1'b0}), .b(register_3_q), .out(adder_3_out), .cin(1'b1), .cout(adder_3_cout));
  Register register_4 (.D(adder_1_out), .en(clock_1_out), .clk(clock_1_out));  // open: Q, clr
  Register register_5 (.D(adder_2_out), .en(clock_1_out), .clk(clock_1_out));  // open: Q, clr
  Register register_6 (.D(adder_3_out), .en(clock_1_out), .clk(clock_1_out));  // open: Q, clr

  // Notes on the sheet:
  //   contents of rom_1 (hex, n*v repeats v):
  //   f d a
endmodule
