// Logisim project buffer_register.circ as structural Verilog: 1 circuit, main circuit main
module main (
);

  wire button_1_out, button_2_out;
  wire [7:0] adder_1_out, controlled_buffer_1_out, register_1_q, register_2_q;

  Button button_1 (.out(button_1_out));
  Button button_2 (.out(button_2_out));
  Register register_1 (.D(adder_1_out), .en(button_1_out), .clk(button_1_out), .Q(register_1_q), .clr(button_2_out));
  Register #(.trigger("high")) register_2 (
    .D(register_1_q), .en(button_1_out), .clk(button_1_out), .Q(register_2_q), .clr(button_2_out));
  Adder adder_1 (.a(8'h5), .b(register_2_q), .out(adder_1_out));  // open: cin, cout
  assign controlled_buffer_1_out = 1'b1 ? register_2_q : 8'bz;  // Controlled_Buffer controlled_buffer_1
  // Probe on controlled_buffer_1_out
endmodule
