// Logisim project output_in_chunks.circ as structural Verilog: 1 circuit, main circuit main
module main (
  input  [31:0] Reg_Input,
  input  Reset_Output_Seq,
  output [3:0] Out_Data_Bits,
  output Have_Output,
  output Done_Output,
  output out_6,
  output out_7
);

  wire Output_Seq_Clk_out, Reset_out, Set_Input_out;
  wire [2:0] counter_1_q;
  wire [31:0] register_1_q;

  Button Reset (.out(Reset_out));
  Button Set_Input (.out(Set_Input_out));
  Clock Output_Seq_Clk (.out(Output_Seq_Clk_out));
  Register #(.width(32)) register_1 (
    .D(Reg_Input), .en(Set_Input_out), .clk(Set_Input_out), .Q(register_1_q), .clr(Reset_out));
  Counter #(.max('h7), .width(3)) counter_1 (
    .clr(Reset_Output_Seq), .load(1'b0), .up(1'b1), .count(Have_Output), .clk(Output_Seq_Clk_out),
    .D(3'b000), .carry(Done_Output), .Q(counter_1_q));
  BitSelector #(.group(4), .width(32)) bitselector_1 (.in(register_1_q), .out(Out_Data_Bits), .sel(counter_1_q));
  D_Flip_Flop d_ff_1 (.D(Set_Input_out), .clk(Set_Input_out), .Q(Have_Output), .reset(Reset_out));  // open: Qn, preset

  // Notes on the sheet:
  //   Reg_Input: initial=0xf0e0d0c
endmodule
