// Logisim project playaround.circ as structural Verilog
module ecksor (
  input  a,
  input  b,
  output x
);

  wire and_1_out, and_2_out, not_1_out, not_2_out;

  not not_1 (not_1_out, a);
  not not_2 (not_2_out, b);
  and and_1 (and_1_out, not_1_out, b);
  and and_2 (and_2_out, a, not_2_out);
  or or_1 (x, and_1_out, and_2_out);
endmodule

module blinking_led (
);

  wire clock_1_out;

  Clock clock_1 (.out(clock_1_out));
  LED led_1 (.in(clock_1_out));
endmodule

module one_bit_half_adder (
  input  a,
  input  b,
  output sum,
  output carry
);

  xor xor_1 (sum, a, b);
  and and_1 (carry, a, b);
endmodule

module one_bit_half_adder_ecksor (
  input  a,
  input  b,
  output sum,
  output carry
);

  and and_1 (carry, a, b);
  ecksor ecksor_1 (.a(a), .b(b), .x(sum));
endmodule

module one_bit_full_adder (
  input  a,
  input  b,
  input  carry_in,
  output sum,
  output carry_out
);

  wire and_1_out, and_2_out, xor_1_out;

  xor xor_1 (xor_1_out, a, b);
  and and_1 (and_1_out, a, b);
  xor xor_2 (sum, xor_1_out, carry_in);
  and and_2 (and_2_out, xor_1_out, carry_in);
  or or_1 (carry_out, and_1_out, and_2_out);
endmodule

module four_bit_full_adder (
  input  a0,
  input  a1,
  input  a2,
  input  a3,
  input  b0,
  input  b1,
  input  b2,
  input  b3,
  output s0,
  output s1,
  output s2,
  output s3,
  output carry
);

  wire one_bit_full_adder_1_carry_out, one_bit_full_adder_2_carry_out, one_bit_full_adder_3_carry_out,
       undriven;

  one_bit_full_adder one_bit_full_adder_1 (
    .a(a0), .b(b0), .carry_in(undriven), .sum(s0), .carry_out(one_bit_full_adder_1_carry_out));
  one_bit_full_adder one_bit_full_adder_2 (
    .a(a1), .b(b1), .carry_in(one_bit_full_adder_1_carry_out), .sum(s1),
    .carry_out(one_bit_full_adder_2_carry_out));
  one_bit_full_adder one_bit_full_adder_3 (
    .a(a2), .b(b2), .carry_in(one_bit_full_adder_2_carry_out), .sum(s2),
    .carry_out(one_bit_full_adder_3_carry_out));
  one_bit_full_adder one_bit_full_adder_4 (
    .a(a3), .b(b3), .carry_in(one_bit_full_adder_3_carry_out), .sum(s3), .carry_out(carry));
endmodule

module add_from_rom (
  input  [7:0] in_1
);

  wire [7:0] rom_1_data;

  ROM rom_1 (.addr(in_1), .data(rom_1_data));
  four_bit_full_adder four_bit_full_adder_1 (
    .a0(rom_1_data[0]), .a1(rom_1_data[1]), .a2(rom_1_data[2]), .a3(rom_1_data[3]), .b0(rom_1_data[4]),
    .b1(rom_1_data[5]), .b2(rom_1_data[6]), .b3(rom_1_data[7]));  // open: s0, s1, s2, s3, carry

  // Notes on the sheet:
  //   contents of rom_1 (hex, n*v repeats v):
  //   0 10 28 0 0 0 f3
endmodule

module buttoned_counter (
  output out_1,
  output out_2,
  output out_3,
  output out_4
);

  wire Count_out, Reset_out;
  wire [3:0] four_bit_full_adder_1_s0;

  Button Count (.out(Count_out));
  Button Reset (.out(Reset_out));
  Register #(.width(4)) register_1 (
    .D(four_bit_full_adder_1_s0), .en(1'b1), .clk(Count_out), .Q({out_4, out_3, out_2, out_1}),
    .clr(Reset_out));
  four_bit_full_adder four_bit_full_adder_1 (
    .a0(out_1), .a1(out_2), .a2(out_3), .a3(out_4), .b0(1'b1), .s0(four_bit_full_adder_1_s0[0]),
    .s1(four_bit_full_adder_1_s0[1]), .s2(four_bit_full_adder_1_s0[2]), .s3(four_bit_full_adder_1_s0[3]));  // open: b1, b2, b3, carry
endmodule

module Four_bit_register (
  input  Clk,
  input  D0,
  input  D1,
  input  D2,
  input  D3,
  output O0,
  output O1,
  output O2,
  output O3
);

  D_Flip_Flop d_ff_1 (.D(D0), .clk(Clk), .Q(O0));  // open: Qn, preset, reset
  D_Flip_Flop d_ff_2 (.D(D1), .clk(Clk), .Q(O1));  // open: Qn, preset, reset
  D_Flip_Flop d_ff_3 (.D(D2), .clk(Clk), .Q(O2));  // open: Qn, preset, reset
  D_Flip_Flop d_ff_4 (.D(D3), .clk(Clk), .Q(O3));  // open: Qn, preset, reset
endmodule

module One_bit_ALU (
  input  [2:0] Op,
  input  Sub,
  input  C_in,
  input  A,
  input  B,
  input  Less,
  output Result,
  output C_out,
  output Set
);

  wire and_1_out, nor_1_out, or_1_out, xor_1_out, xor_2_out;

  xor xor_1 (xor_1_out, B, Sub);
  and and_1 (and_1_out, A, B);
  or or_1 (or_1_out, A, B);
  nor nor_1 (nor_1_out, A, B);
  xor xor_2 (xor_2_out, A, B);
  Adder #(.width(1)) adder_1 (.a(A), .b(xor_1_out), .out(Set), .cin(C_in), .cout(C_out));
  Multiplexer #(.select(3)) multiplexer_1 (
    .in0(and_1_out), .in1(or_1_out), .in2(nor_1_out), .in3(xor_2_out), .in4(Set), .in5(Less), .out(Result),
    .sel(Op));  // open: in6, in7
endmodule

module Eight_bit_ALU (
  input  Sub,
  input  [2:0] Op,
  input  [7:0] A,
  input  [7:0] B,
  output [7:0] Result,
  output Carry,
  output Zero
);

  wire one_bit_alu_1_c_out, one_bit_alu_2_c_out, one_bit_alu_3_c_out, one_bit_alu_4_c_out,
       one_bit_alu_5_c_out, one_bit_alu_6_c_out, one_bit_alu_7_c_out, one_bit_alu_8_set;

  One_bit_ALU one_bit_alu_1 (
    .Op(Op), .Sub(Sub), .C_in(Sub), .A(A[0]), .B(B[0]), .Less(one_bit_alu_8_set), .Result(Result[0]),
    .C_out(one_bit_alu_1_c_out));  // open: Set
  One_bit_ALU one_bit_alu_2 (
    .Op(Op), .Sub(Sub), .C_in(one_bit_alu_1_c_out), .A(A[1]), .B(B[1]), .Less(1'b0), .Result(Result[1]),
    .C_out(one_bit_alu_2_c_out));  // open: Set
  One_bit_ALU one_bit_alu_3 (
    .Op(Op), .Sub(Sub), .C_in(one_bit_alu_2_c_out), .A(A[2]), .B(B[2]), .Less(1'b0), .Result(Result[2]),
    .C_out(one_bit_alu_3_c_out));  // open: Set
  One_bit_ALU one_bit_alu_4 (
    .Op(Op), .Sub(Sub), .C_in(one_bit_alu_3_c_out), .A(A[3]), .B(B[3]), .Less(1'b0), .Result(Result[3]),
    .C_out(one_bit_alu_4_c_out));  // open: Set
  One_bit_ALU one_bit_alu_5 (
    .Op(Op), .Sub(Sub), .C_in(one_bit_alu_4_c_out), .A(A[4]), .B(B[4]), .Less(1'b0), .Result(Result[4]),
    .C_out(one_bit_alu_5_c_out));  // open: Set
  One_bit_ALU one_bit_alu_6 (
    .Op(Op), .Sub(Sub), .C_in(one_bit_alu_5_c_out), .A(A[5]), .B(B[5]), .Less(1'b0), .Result(Result[5]),
    .C_out(one_bit_alu_6_c_out));  // open: Set
  One_bit_ALU one_bit_alu_7 (
    .Op(Op), .Sub(Sub), .C_in(one_bit_alu_6_c_out), .A(A[6]), .B(B[6]), .Less(1'b0), .Result(Result[6]),
    .C_out(one_bit_alu_7_c_out));  // open: Set
  One_bit_ALU one_bit_alu_8 (
    .Op(Op), .Sub(Sub), .C_in(one_bit_alu_7_c_out), .A(A[7]), .B(B[7]), .Less(1'b0), .Result(Result[7]),
    .C_out(Carry), .Set(one_bit_alu_8_set));
  nor nor_1 (Zero, Result[0], Result[1], Result[2], Result[3], Result[4], Result[5], Result[6], Result[7]);
endmodule
