// Logisim project screen_filler.circ as structural Verilog: 1 circuit, main circuit main
module main (
  input  [7:0] in_1,
  input  [7:0] in_2,
  input  [7:0] in_3
);

  wire button_1_out, clock_1_out;
  wire [13:0] counter_1_q;

  Button button_1 (.out(button_1_out));
  Clock clock_1 (.out(clock_1_out));
  Counter #(.max('h3fff), .width(14)) counter_1 (
    .clr(button_1_out), .up(1'b1), .count(1'b1), .clk(clock_1_out), .Q(counter_1_q));  // open: load, D, carry
  // RGB_Video rgb_video_1: pin names not known; wires that end beside it: button_1_out, clock_1_out, clock_1_out, counter_1_q[6:0], counter_1_q[13:7], {in_3, in_2, in_1}
endmodule
